// Logisim project Logical.circ as structural Verilog: 1 circuit, main circuit main
module main (
  input  A1,
  input  A2,
  input  A4,
  input  A8,
  input  B1,
  input  B2,
  input  B4,
  input  B8,
  output Y1,
  output Y2,
  output Y4,
  output Y8
);

  // DIP_7432 dip_7432_1: pin names not known; wires that end beside it: A1, B1, Y1, A2, B2, Y2, A4, B4, Y4, A8, B8, Y8
endmodule
