// Logisim project alu.circ as structural Verilog: 1 circuit, main circuit main
module main (
  input  A1,
  input  A2,
  input  A4,
  input  A8,
  input  B1,
  input  B2,
  input  B4,
  input  B8,
  input  C0,
  input  C1,
  input  C2,
  output Y1,
  output Y2,
  output Y4,
  output Y8,
  output C,
  output S,
  output V,
  output Z
);

  wire dip_7432_1_p3, dip_7432_1_p4, dip_7432_1_p5, dip_7432_1_p6, dip_74157_1_p1, main_1_c, main_1_v,
       main_1_y1, main_1_y2, main_1_y4, main_1_y8, main_2_y1, main_2_y2, main_2_y4, main_2_y8;

  arithmatic_main main_1 (
    .A1(A1), .A2(A2), .A4(A4), .A8(A8), .B1(B1), .B2(B2), .B4(B4), .B8(B8), .GND(1'b0), .VCC(1'b1), .C0(C0),
    .C1(C1), .C2(C2), .Y1(main_1_y1), .Y2(main_1_y2), .Y4(main_1_y4), .Y8(main_1_y8), .C(main_1_c),
    .V(main_1_v));
  Logical_main main_2 (
    .A1(A1), .A2(A2), .A4(A4), .A8(A8), .B1(B1), .B2(B2), .B4(B4), .B8(B8), .Y1(main_2_y1), .Y2(main_2_y2),
    .Y4(main_2_y4), .Y8(main_2_y8));
  // DIP_7432 dip_7432_1: pin names not known; wires that end beside it: C0, C2, dip_7432_1_p3, dip_7432_1_p4, dip_7432_1_p5, dip_7432_1_p6, Y1, Y2, dip_7432_1_p4, Y4, S, dip_7432_1_p5
  // DIP_74157 dip_74157_1: pin names not known; wires that end beside it: dip_74157_1_p1, main_1_y1, main_2_y1, Y1, main_1_y2, main_2_y2, Y2, 1'b0, main_1_y4, main_2_y4, Y4, main_1_y8, main_2_y8, S
  // DIP_7404 dip_7404_1: pin names not known; wires that end beside it: dip_7432_1_p3, dip_74157_1_p1, dip_7432_1_p6, Z
  // DIP_7408 dip_7408_1: pin names not known; wires that end beside it: dip_7432_1_p3, main_1_c, C, dip_7432_1_p3, main_1_v, V

  assign Y8 = S;
endmodule
