// Logisim project arithmatic.circ as structural Verilog: 1 circuit, main circuit main
module main (
  input  A1,
  input  A2,
  input  A4,
  input  A8,
  input  B1,
  input  B2,
  input  B4,
  input  B8,
  input  GND,
  input  VCC,
  input  C0,
  input  C1,
  input  C2,
  output Y1,
  output Y2,
  output Y4,
  output Y8,
  output C,
  output V
);

  wire dip_7404_1_p2, dip_7404_1_p4, dip_7404_1_p6, dip_7404_1_p8, dip_7404_2_p2, dip_7404_2_p4,
       dip_7404_2_p6, dip_7404_2_p8, dip_74157_1_p4, dip_74157_1_p7, dip_74157_1_p11, dip_74157_1_p14,
       dip_74157_2_p1, dip_74157_2_p4, dip_74157_2_p7, dip_74157_2_p11, dip_74157_2_p14,
       multiplexer_for_A_p5, multiplexer_for_Carry_p5, xor_p3, xor_p6;

  // DIP_7404 dip_7404_1: pin names not known; wires that end beside it: B1, dip_7404_1_p2, B2, dip_7404_1_p4, B4, dip_7404_1_p6, B8, dip_7404_1_p8
  // DIP_7404 dip_7404_2: pin names not known; wires that end beside it: A1, dip_7404_2_p2, A2, dip_7404_2_p4, A4, dip_7404_2_p6, A8, dip_7404_2_p8
  // DIP_74151 multiplexer_for_A: pin names not known; wires that end beside it: GND, GND, VCC, GND, multiplexer_for_A_p5, GND, GND, GND, GND, GND, C0, C1, C2
  // DIP_74157 dip_74157_1: pin names not known; wires that end beside it: multiplexer_for_A_p5, A1, dip_7404_2_p2, dip_74157_1_p4, A2, dip_7404_2_p4, dip_74157_1_p7, GND, A4, dip_7404_2_p6, dip_74157_1_p11, A8, dip_7404_2_p8, dip_74157_1_p14
  // DIP_74157 dip_74157_2: pin names not known; wires that end beside it: dip_74157_2_p1, GND, dip_7404_1_p2, dip_74157_2_p4, GND, dip_7404_1_p4, dip_74157_2_p7, GND, GND, dip_7404_1_p6, dip_74157_2_p11, GND, dip_7404_1_p8, dip_74157_2_p14
  // DIP_74151 multiplexer_for_B: pin names not known; wires that end beside it: VCC, GND, GND, GND, dip_74157_2_p1, GND, GND, VCC, GND, GND, C0, C1, C2
  // DIP_74151 multiplexer_for_Carry: pin names not known; wires that end beside it: VCC, GND, GND, GND, multiplexer_for_Carry_p5, GND, VCC, GND, GND, GND, C0, C1, C2
  // _7483 7483_1: pin names not known; wires that end beside it: dip_74157_1_p7, Y1, dip_74157_2_p7, dip_74157_1_p4, Y2, dip_74157_2_p4, dip_74157_2_p11, multiplexer_for_Carry_p5, dip_74157_1_p11, C, Y4, Y8, dip_74157_1_p14, dip_74157_2_p14
  // DIP_7486 xor: pin names not known; wires that end beside it: C, Y8, xor_p3, xor_p3, dip_74157_2_p14, xor_p6, dip_74157_1_p14, xor_p6, V
endmodule
