// Logisim project A1_Group2.circ as structural Verilog: 8 circuits, main circuit main
module main (
  input  [31:0] A,
  input  [31:0] B,
  input  [4:0] rshift_dist,
  output isOverflow,
  output [11:0] exp_after_normal,
  output isUnderflow,
  output [19:0] rounded_significand,
  output sign,
  output isOverflow_2,
  output isUnderflow_2
);

  wire bitfinder_1_found;
  wire [4:0] bitfinder_1_index, subtractor_1_out;
  wire [11:0] adder_1_out, bit_extender_1_out, bit_extender_2_out, bit_extender_3_out,
       find_exp_add_significand_1_result_exp, multiplexer_1_out, subtractor_2_out;
  wire [19:0] rounding_1_rounded_significand, rounding_2_rounded_significand;
  wire [20:20] find_exp_add_significand_1_result_significand_2;
  wire [21:0] find_exp_add_significand_1_result_significand;
  wire [22:0] shifter_1_out, shifter_2_out;

  find_exp_add_significand find_exp_add_significand_1 (
    .A(A), .B(B), .result_exp(find_exp_add_significand_1_result_exp),
    .result_significand({find_exp_add_significand_1_result_significand[21:20], find_exp_add_significand_1_result_significand_2[20], find_exp_add_significand_1_result_significand[19:0]}),
    .result_sign(sign));
  BitFinder #(.width(23)) bitfinder_1 (
    .in({find_exp_add_significand_1_result_significand[0], find_exp_add_significand_1_result_significand[1], find_exp_add_significand_1_result_significand[2], find_exp_add_significand_1_result_significand[3], find_exp_add_significand_1_result_significand[4], find_exp_add_significand_1_result_significand[5], find_exp_add_significand_1_result_significand[6], find_exp_add_significand_1_result_significand[7], find_exp_add_significand_1_result_significand[8], find_exp_add_significand_1_result_significand[9], find_exp_add_significand_1_result_significand[10], find_exp_add_significand_1_result_significand[11], find_exp_add_significand_1_result_significand[12], find_exp_add_significand_1_result_significand[13], find_exp_add_significand_1_result_significand[14], find_exp_add_significand_1_result_significand[15], find_exp_add_significand_1_result_significand[16], find_exp_add_significand_1_result_significand[17], find_exp_add_significand_1_result_significand[18], find_exp_add_significand_1_result_significand[19], find_exp_add_significand_1_result_significand_2[20], find_exp_add_significand_1_result_significand[20], find_exp_add_significand_1_result_significand[21]}),
    .index(bitfinder_1_index), .found(bitfinder_1_found));
  Shifter #(.width(23), .shift("lr")) shifter_1 (
    .in({find_exp_add_significand_1_result_significand[21:20], find_exp_add_significand_1_result_significand_2[20], find_exp_add_significand_1_result_significand[19:0]}),
    .\dist (rshift_dist), .out(shifter_1_out));
  assign bit_extender_1_out = {{7{1'b0}}, bitfinder_1_index};  // Bit_Extender bit_extender_1
  Shifter #(.width(23)) shifter_2 (
    .in({find_exp_add_significand_1_result_significand[21:20], find_exp_add_significand_1_result_significand_2[20], find_exp_add_significand_1_result_significand[19:0]}),
    .\dist (bitfinder_1_index), .out(shifter_2_out));
  assign bit_extender_2_out = {{7{1'b0}}, rshift_dist};  // Bit_Extender bit_extender_2
  Multiplexer #(.width(12), .enable("false")) multiplexer_1 (
    .in0(bit_extender_1_out), .in1(bit_extender_3_out), .out(multiplexer_1_out), .sel(bitfinder_1_found));
  Subtractor #(.width(5)) subtractor_1 (
    .a(bitfinder_1_index), .b(5'b00011), .out(subtractor_1_out), .bin(1'b0));  // open: bout
  assign bit_extender_3_out = {{7{1'b0}}, subtractor_1_out};  // Bit_Extender bit_extender_3
  Subtractor #(.width(12)) subtractor_2 (
    .a(find_exp_add_significand_1_result_exp), .b(multiplexer_1_out), .out(subtractor_2_out), .bin(1'b0));  // open: bout
  Adder #(.width(12)) adder_1 (
    .a(find_exp_add_significand_1_result_exp), .b(bit_extender_2_out), .out(adder_1_out), .cin(1'b0));  // open: cout
  check_overflow_underflow check_overflow_underflow_1 (
    .Exp(subtractor_2_out), .overflow(isOverflow), .underflow(isUnderflow));
  check_overflow_underflow check_overflow_underflow_2 (
    .Exp(adder_1_out), .overflow(isOverflow_2), .underflow(isUnderflow_2));
  rounding rounding_1 (
    .input_significand(shifter_2_out), .rounded_significand(rounding_1_rounded_significand));  // open: truncated, round_up, round_to_even
  rounding rounding_2 (
    .input_significand(shifter_1_out), .rounded_significand(rounding_2_rounded_significand));  // open: truncated, round_up, round_to_even
  Multiplexer #(.width(12), .enable("false")) multiplexer_2 (
    .in0(subtractor_2_out), .in1(adder_1_out), .out(exp_after_normal),
    .sel(find_exp_add_significand_1_result_significand_2[20]));
  Multiplexer #(.width(20), .enable("false")) multiplexer_3 (
    .in0(rounding_1_rounded_significand), .in1(rounding_2_rounded_significand), .out(rounded_significand),
    .sel(find_exp_add_significand_1_result_significand_2[20]));

  // Notes on the sheet:
  //   base = 2047 = 0b0111 1111 1111
  //   31->sign, (30-19)->(actual_exp + bias), (18-0)->fraction
endmodule

module Comp_exp (
  input  [11:0] Exp_A,
  input  [11:0] Exp_B,
  output X__Y,
  output X_Y,
  output [11:0] Diff,
  output b_out,
  output [11:0] Larger
);

  wire comparator_1_eq, comparator_1_gt;
  wire [11:0] multiplexer_2_out;

  Comparator #(.width(12), .mode("unsigned")) comparator_1 (
    .a(Exp_A), .b(Exp_B), .gt(comparator_1_gt), .eq(comparator_1_eq), .lt(X_Y));
  or or_1 (X__Y, comparator_1_gt, comparator_1_eq);
  Multiplexer #(.width(12), .enable("false")) multiplexer_1 (.in0(Exp_A), .in1(Exp_B), .out(Larger), .sel(X_Y));
  Multiplexer #(.width(12), .enable("false")) multiplexer_2 (
    .in0(Exp_A), .in1(Exp_B), .out(multiplexer_2_out), .sel(X__Y));
  Subtractor #(.width(12)) subtractor_1 (.a(Larger), .b(multiplexer_2_out), .out(Diff), .bin(1'b0), .bout(b_out));
endmodule

module shift_fraction (
  input  [22:0] Significand_A,
  input  [22:0] Significand_B,
  input  s_l,
  input  s_s,
  input  [4:0] shift_amount,
  output A__B,
  output [22:0] Significand_larger,
  output [22:0] Significand_smaller
);

  wire comparator_1_eq, comparator_1_gt;
  wire [22:0] multiplexer_2_out;

  Comparator #(.width(23), .mode("unsigned")) comparator_1 (
    .a(Significand_A), .b(Significand_B), .gt(comparator_1_gt), .eq(comparator_1_eq));  // open: lt
  Multiplexer #(.width(23), .enable("false")) multiplexer_1 (
    .in0(Significand_A), .in1(Significand_B), .out(Significand_larger), .sel(s_l));
  Multiplexer #(.width(23), .enable("false")) multiplexer_2 (
    .in0(Significand_A), .in1(Significand_B), .out(multiplexer_2_out), .sel(s_s));
  or or_1 (A__B, comparator_1_gt, comparator_1_eq);
  Shifter #(.width(23), .shift("lr")) shifter_1 (
    .in(multiplexer_2_out), .\dist (shift_amount), .out(Significand_smaller));
endmodule

module adjust_input_sign (
  input  [22:0] unsigned_part,
  input  Sign_bit,
  output [22:0] complemented
);

  wire [22:0] negator_1_out;

  Negator #(.width(23)) negator_1 (.in(unsigned_part), .out(negator_1_out));
  Multiplexer #(.width(23), .enable("false")) multiplexer_1 (
    .in0(unsigned_part), .in1(negator_1_out), .out(complemented), .sel(Sign_bit));
endmodule

module negate_result (
  input  [22:0] initial_result,
  input  isComplemented,
  output [22:0] final_result
);

  wire [22:0] negator_1_out;

  Negator #(.width(23)) negator_1 (.in(initial_result), .out(negator_1_out));
  Multiplexer #(.width(23), .enable("false")) multiplexer_1 (
    .in0(initial_result), .in1(negator_1_out), .out(final_result), .sel(isComplemented));
endmodule

module check_overflow_underflow (
  input  [11:0] Exp,
  output overflow,
  output underflow
);

  Comparator #(.width(12), .mode("unsigned")) comparator_1 (.a(Exp), .b(12'hffe), .gt(overflow));  // open: eq, lt
  Comparator #(.width(12), .mode("unsigned")) comparator_2 (.a(Exp), .b(12'h1), .lt(underflow));  // open: gt, eq
endmodule

module rounding (
  input  [22:0] input_significand,
  output [19:0] rounded_significand,
  output [19:0] truncated,
  output [19:0] round_up,
  output [19:0] round_to_even
);

  Multiplexer #(.select(3), .width(20), .enable("false")) multiplexer_1 (
    .in0(input_significand[22:3]), .in1(input_significand[22:3]), .in2(input_significand[22:3]),
    .in3(input_significand[22:3]), .in4(round_to_even), .in5(round_up), .in6(round_up), .in7(round_up),
    .out(rounded_significand), .sel(input_significand[2:0]));
  Adder #(.width(20)) adder_1 (.a(input_significand[22:3]), .b(20'h1), .out(round_up), .cin(1'b0));  // open: cout
  assign round_to_even = input_significand[22:3] & 20'hffffe;  // AND_Gate and_1, 20 bits wide

  assign truncated = input_significand[22:3];

  // Notes on the sheet:
  //   0->S, 1->R, 2->G
endmodule

module find_exp_add_significand (
  input  [31:0] A,
  input  [31:0] B,
  output [11:0] result_exp,
  output [22:0] result_significand,
  output result_sign
);

  wire and_1_out, and_2_out, and_3_out, comp_exp_1_b_out, comp_exp_1_x__y, comp_exp_1_x_y, not_1_out,
       not_2_out, or_1_out, shift_fraction_1_a__b;
  wire [11:0] comp_exp_1_diff;
  wire [22:0] adder_1_out, adjust_input_sign_1_complemented, adjust_input_sign_2_complemented,
       shift_fraction_1_significand_larger, shift_fraction_1_significand_smaller;

  Comp_exp comp_exp_1 (
    .Exp_A(A[30:19]), .Exp_B(B[30:19]), .X__Y(comp_exp_1_x__y), .X_Y(comp_exp_1_x_y), .Diff(comp_exp_1_diff),
    .b_out(comp_exp_1_b_out), .Larger(result_exp));
  and and_1 (and_1_out, shift_fraction_1_a__b, not_1_out);
  not not_1 (not_1_out, comp_exp_1_b_out);
  or or_1 (or_1_out, and_1_out, comp_exp_1_b_out);
  shift_fraction shift_fraction_1 (
    .s_l(comp_exp_1_x_y), .s_s(comp_exp_1_x__y), .Significand_A({4'b0001, A[18:0]}),
    .Significand_B({4'b0001, B[18:0]}), .shift_amount(comp_exp_1_diff[4:0]), .A__B(shift_fraction_1_a__b),
    .Significand_larger(shift_fraction_1_significand_larger),
    .Significand_smaller(shift_fraction_1_significand_smaller));
  and and_2 (and_2_out, or_1_out, A[31]);
  and and_3 (and_3_out, B[31], not_2_out);
  not not_2 (not_2_out, or_1_out);
  adjust_input_sign adjust_input_sign_1 (
    .unsigned_part(shift_fraction_1_significand_smaller), .Sign_bit(A[31]),
    .complemented(adjust_input_sign_1_complemented));
  adjust_input_sign adjust_input_sign_2 (
    .unsigned_part(shift_fraction_1_significand_larger), .Sign_bit(B[31]),
    .complemented(adjust_input_sign_2_complemented));
  or or_2 (result_sign, and_2_out, and_3_out);
  Adder #(.width(23)) adder_1 (
    .a(adjust_input_sign_1_complemented), .b(adjust_input_sign_2_complemented), .out(adder_1_out), .cin(1'b0));  // open: cout
  negate_result negate_result_1 (
    .initial_result(adder_1_out), .isComplemented(result_sign), .final_result(result_significand));
endmodule
